// Logisim project Group5_PartA.circ as structural Verilog: 5 circuits, main circuit Reg16bit
module Reg16bit (
  input  [15:0] Din,
  input  OE,
  input  clk,
  input  we,
  input  Reset,
  output [15:0] Dout,
  output [15:0] Result,
  output [7:0] LSB,
  output [7:0] MSB
);

  Register #(.width(16)) register_1 (.D(Din), .en(we), .clk(clk), .Q(Result), .clr(Reset));
  assign Dout = OE ? Result : 16'bz;  // Controlled_Buffer controlled_buffer_1
  BitSelector #(.group(8), .width(16)) bitselector_1 (.in(Result), .out(LSB), .sel(1'b0));
  BitSelector #(.group(8), .width(16)) bitselector_2 (.in(Result), .out(MSB), .sel(1'b1));

  // Notes on the sheet:
  //   constant value 0x0
  //   constant value 0x1
endmodule

module project_ro (
  input  [15:0] A,
  input  [15:0] B,
  input  [2:0] RU_Selector,
  output RU_Result
);

  wire comparator_1_eq, comparator_1_gt, comparator_1_lt, not_1_out, or_1_out, or_2_out;

  Comparator #(.width(16)) comparator_1 (
    .a(A), .b(B), .gt(comparator_1_gt), .eq(comparator_1_eq), .lt(comparator_1_lt));
  or or_1 (or_1_out, comparator_1_gt, comparator_1_eq);
  or or_2 (or_2_out, comparator_1_lt, comparator_1_eq);
  not not_1 (not_1_out, comparator_1_eq);
  Multiplexer #(.select(3)) multiplexer_1 (
    .in0(comparator_1_gt), .in1(comparator_1_eq), .in2(or_1_out), .in3(comparator_1_lt), .in4(or_2_out),
    .in5(not_1_out), .out(RU_Result), .sel(RU_Selector));  // open: in6, in7

  // Notes on the sheet:
  //   >
  //   >=
  //   <
  //   <=
  //   ==
  //   !-
endmodule

module project_ao (
  input  [15:0] A,
  input  [15:0] B,
  input  [3:0] AUselector,
  output [15:0] AU_Result,
  output [15:0] AU_Dout
);

  wire [15:0] adder_1_out, adder_2_out, and_1_out, divider_1_out, divider_1_rem, multiplexer_1_out,
       multiplier_1_out, negator_1_out, negator_2_out, not_1_out, or_1_out, shifter_1_out, shifter_2_out,
       shifter_3_out, shifter_4_out, xor_1_out;

  Adder #(.width(16)) adder_1 (.a(A), .b(A), .out(adder_1_out));  // open: cin, cout
  assign and_1_out = A & A;  // AND_Gate and_1, 16 bits wide
  assign or_1_out = A | A;  // OR_Gate or_1, 16 bits wide
  Divider #(.width(16)) divider_1 (.a(A), .b(A), .out(divider_1_out), .rem(divider_1_rem));  // open: upper
  Multiplier #(.width(16)) multiplier_1 (.a(A), .b(A), .out(multiplier_1_out));  // open: cin, cout
  assign not_1_out = ~A;  // NOT_Gate not_1, 16 bits wide
  assign xor_1_out = A ^ A;  // XOR_Gate xor_1, 16 bits wide
  Multiplexer #(.width(16)) multiplexer_1 (
    .in0(divider_1_out), .in1(divider_1_rem), .out(multiplexer_1_out), .sel(AUselector[0]));
  Adder #(.width(16)) adder_2 (.a(A), .b(not_1_out), .out(adder_2_out), .cin(1'b1));  // open: cout
  Shifter #(.width(16)) shifter_1 (.in(A), .\dist (4'b0010), .out(shifter_1_out));
  Shifter #(.width(16)) shifter_2 (.in(A), .\dist (4'b0010), .out(shifter_2_out));
  Negator #(.width(16)) negator_1 (.in(A), .out(negator_1_out));
  Negator #(.width(16)) negator_2 (.in(A), .out(negator_2_out));
  Shifter #(.width(16)) shifter_3 (.in(A), .\dist (4'b0010), .out(shifter_3_out));
  Shifter #(.width(16)) shifter_4 (.in(A), .\dist (4'b0010), .out(shifter_4_out));
  Multiplexer #(.select(4), .width(16)) multiplexer_2 (
    .in0(adder_1_out), .in1(and_1_out), .in2(or_1_out), .in3(xor_1_out), .in4(multiplexer_1_out),
    .in5(multiplexer_1_out), .in6(multiplier_1_out), .in7(adder_2_out), .in8(shifter_1_out),
    .in9(shifter_2_out), .in10(shifter_3_out), .in11(shifter_4_out), .in12(negator_1_out),
    .in13(negator_2_out), .out(AU_Dout), .sel(AUselector));  // open: in14, in15

  assign AU_Result = AU_Dout;
  assign B = A;

  // Notes on the sheet:
  //   16-BIT ALU
endmodule

module project_alu (
  input  [15:0] A,
  input  [15:0] B,
  input  [3:0] AU_selector,
  input  [2:0] RU_Selector,
  output [15:0] AU_Result,
  output [15:0] AU_Dout,
  output RU_Result
);

  project_ao project_ao_1 (.A(A), .B(B), .AUselector(AU_selector), .AU_Result(AU_Result), .AU_Dout(AU_Dout));
  project_ro project_ro_1 (.A(A), .B(B), .RU_Selector(RU_Selector), .RU_Result(RU_Result));

  // Notes on the sheet:
  //   16 BITS ALU
endmodule

module Datapath (
  input  in_1,
  input  [3:0] in_2,
  input  [7:0] Test_data,
  input  OE,
  input  [1:0] AU_SELECTOR,
  input  [2:0] LU_SELECTOR,
  output [3:0] out_7,
  output [3:0] counter_content,
  output [7:0] out_9,
  output [7:0] out_10,
  output [7:0] out_11,
  output [7:0] out_12,
  output COUT,
  output [7:0] AU_RESULT,
  output ALU_RESULT,
  output [2:0] SC_O
);

  wire A_p1, A_p4, alu_1_p3, alu_1_p4, B_p2, CLK_out, cu_1_p8, cu_1_p9, cu_1_p10, cu_1_p11, cu_1_p13,
       cu_1_p16, MAR_p2, MAR_p3, MBR_p2, MBR_p3, OUTPUT_REGISTER_p2, OUTPUT_REGISTER_p3;
  wire [3:0] bitselector_2_out, controlled_buffer_1_out, decimal_decoder_1_p1_3, decimal_decoder_2_p1_3,
       decimal_decoder_4_p2_3, MAR_p5;
  wire [7:0] A_p2, bit_extender_1_out, bit_extender_2_out, ram_1_dout, undriven;
  wire [15:0] decimal_decoder_1_p1, decimal_decoder_2_p1, decimal_decoder_3_p2, decimal_decoder_3_p2_2,
       decimal_decoder_4_p2, decimal_decoder_5_p2, decimal_decoder_5_p2_2;
  wire [27:16] decimal_decoder_1_p1_2, decimal_decoder_2_p1_2, decimal_decoder_4_p2_2;

  Clock CLK (.out(CLK_out));
  Counter #(.max('h3), .width(4)) PC (
    .count(cu_1_p9), .clk(CLK_out), .D(controlled_buffer_1_out), .Q(counter_content));  // open: clr, load, up, carry
  assign controlled_buffer_1_out = cu_1_p8 ? counter_content : 4'bz;  // Controlled_Buffer controlled_buffer_1
  // reg8bits A: pin names not known; wires that end beside it: A_p1, A_p2, CLK_out, A_p4, A_p2, out_11, out_11
  // ALU alu_1: pin names not known; wires that end beside it: AU_SELECTOR, out_11, alu_1_p3, alu_1_p4, LU_SELECTOR, COUT, AU_RESULT, A_p2, ALU_RESULT
  // reg8bits B: pin names not known; wires that end beside it: CLK_out, B_p2, A_p2, alu_1_p4, alu_1_p4
  BitSelector #(.group(4)) bitselector_1 (.in(undriven), .out(controlled_buffer_1_out), .sel(1'b0));
  assign bit_extender_1_out = {{4{1'b0}}, counter_content};  // Bit_Extender bit_extender_1
  // Decimal_Decoder decimal_decoder_1: pin names not known; wires that end beside it: {decimal_decoder_1_p1_3, decimal_decoder_1_p1_2, decimal_decoder_1_p1}
  _7_Segment_Display u_7_segment_display_1 (
    .g(decimal_decoder_1_p1[15]), .f(decimal_decoder_1_p1[14]), .a(decimal_decoder_1_p1[13]),
    .b(decimal_decoder_1_p1[12]), .e(decimal_decoder_1_p1_3[3]), .d(decimal_decoder_1_p1_3[2]),
    .c(decimal_decoder_1_p1_3[1]), .dp(decimal_decoder_1_p1_3[0]));
  _7_Segment_Display u_7_segment_display_2 (
    .g(decimal_decoder_1_p1[11]), .f(decimal_decoder_1_p1[10]), .a(decimal_decoder_1_p1[9]),
    .b(decimal_decoder_1_p1[8]), .e(decimal_decoder_1_p1_2[27]), .d(decimal_decoder_1_p1_2[26]),
    .c(decimal_decoder_1_p1_2[25]), .dp(decimal_decoder_1_p1_2[24]));
  // Decimal_Decoder decimal_decoder_2: pin names not known; wires that end beside it: {decimal_decoder_2_p1_3, decimal_decoder_2_p1_2, decimal_decoder_2_p1}
  _7_Segment_Display u_7_segment_display_3 (
    .g(decimal_decoder_2_p1[15]), .f(decimal_decoder_2_p1[14]), .a(decimal_decoder_2_p1[13]),
    .b(decimal_decoder_2_p1[12]), .e(decimal_decoder_2_p1_3[3]), .d(decimal_decoder_2_p1_3[2]),
    .c(decimal_decoder_2_p1_3[1]), .dp(decimal_decoder_2_p1_3[0]));
  _7_Segment_Display u_7_segment_display_4 (
    .g(decimal_decoder_2_p1[11]), .f(decimal_decoder_2_p1[10]), .a(decimal_decoder_2_p1[9]),
    .b(decimal_decoder_2_p1[8]), .e(decimal_decoder_2_p1_2[27]), .d(decimal_decoder_2_p1_2[26]),
    .c(decimal_decoder_2_p1_2[25]), .dp(decimal_decoder_2_p1_2[24]));
  // Decimal_Decoder decimal_decoder_3: pin names not known; wires that end beside it: bit_extender_1_out, {decimal_decoder_3_p2_2, decimal_decoder_3_p2}
  _7_Segment_Display u_7_segment_display_5 (
    .g(decimal_decoder_3_p2[3]), .f(decimal_decoder_3_p2[2]), .a(decimal_decoder_3_p2[1]),
    .b(decimal_decoder_3_p2[0]), .e(decimal_decoder_3_p2_2[3]), .d(decimal_decoder_3_p2_2[2]),
    .c(decimal_decoder_3_p2_2[1]), .dp(decimal_decoder_3_p2_2[0]));
  _7_Segment_Display u_7_segment_display_6 (
    .g(decimal_decoder_1_p1[7]), .f(decimal_decoder_1_p1[6]), .a(decimal_decoder_1_p1[5]),
    .b(decimal_decoder_1_p1[4]), .e(decimal_decoder_1_p1_2[23]), .d(decimal_decoder_1_p1_2[22]),
    .c(decimal_decoder_1_p1_2[21]), .dp(decimal_decoder_1_p1_2[20]));
  _7_Segment_Display u_7_segment_display_7 (
    .g(decimal_decoder_2_p1[7]), .f(decimal_decoder_2_p1[6]), .a(decimal_decoder_2_p1[5]),
    .b(decimal_decoder_2_p1[4]), .e(decimal_decoder_2_p1_2[23]), .d(decimal_decoder_2_p1_2[22]),
    .c(decimal_decoder_2_p1_2[21]), .dp(decimal_decoder_2_p1_2[20]));
  LED led_1 (.in(A_p2[7]));
  assign A_p2 = OE ? Test_data : 8'bz;  // Controlled_Buffer controlled_buffer_2
  _7_Segment_Display u_7_segment_display_8 (
    .g(decimal_decoder_1_p1[3]), .f(decimal_decoder_1_p1[2]), .a(decimal_decoder_1_p1[1]),
    .b(decimal_decoder_1_p1[0]), .e(decimal_decoder_1_p1_2[19]), .d(decimal_decoder_1_p1_2[18]),
    .c(decimal_decoder_1_p1_2[17]), .dp(decimal_decoder_1_p1_2[16]));
  _7_Segment_Display u_7_segment_display_9 (
    .g(decimal_decoder_2_p1[3]), .f(decimal_decoder_2_p1[2]), .a(decimal_decoder_2_p1[1]),
    .b(decimal_decoder_2_p1[0]), .e(decimal_decoder_2_p1_2[19]), .d(decimal_decoder_2_p1_2[18]),
    .c(decimal_decoder_2_p1_2[17]), .dp(decimal_decoder_2_p1_2[16]));
  LED led_2 (.in(A_p2[6]));
  LED led_3 (.in(A_p2[5]));
  LED led_4 (.in(A_p2[4]));
  LED led_5 (.in(A_p2[3]));
  LED led_6 (.in(A_p2[2]));
  LED led_7 (.in(A_p2[1]));
  LED led_8 (.in(A_p2[0]));
  assign A_p2 = cu_1_p13 ? out_10 : 8'bz;  // Controlled_Buffer controlled_buffer_3
  // reg4bits MAR: pin names not known; wires that end beside it: controlled_buffer_1_out, MAR_p2, MAR_p3, CLK_out, MAR_p5, out_7
  Counter #(.max('h5), .width(3)) STEP_COUNTER (.clk(CLK_out), .Q(SC_O));  // open: clr, load, up, count, D, carry
  _7_Segment_Display u_7_segment_display_10 (
    .g(decimal_decoder_4_p2[15]), .f(decimal_decoder_4_p2[14]), .a(decimal_decoder_4_p2[13]),
    .b(decimal_decoder_4_p2[12]), .e(decimal_decoder_4_p2_3[3]), .d(decimal_decoder_4_p2_3[2]),
    .c(decimal_decoder_4_p2_3[1]), .dp(decimal_decoder_4_p2_3[0]));
  BitSelector #(.group(4)) bitselector_2 (.in(out_9), .out(bitselector_2_out), .sel(1'b1));
  // reg8bits MBR: pin names not known; wires that end beside it: CLK_out, MBR_p2, MBR_p3, A_p2, out_10, A_p2
  // reg8bits OUTPUT_REGISTER: pin names not known; wires that end beside it: CLK_out, OUTPUT_REGISTER_p2, OUTPUT_REGISTER_p3, A_p2, out_12, A_p2
  // Decimal_Decoder decimal_decoder_4: pin names not known; wires that end beside it: out_12, {decimal_decoder_4_p2_3, decimal_decoder_4_p2_2, decimal_decoder_4_p2}
  _7_Segment_Display u_7_segment_display_11 (
    .g(decimal_decoder_4_p2[11]), .f(decimal_decoder_4_p2[10]), .a(decimal_decoder_4_p2[9]),
    .b(decimal_decoder_4_p2[8]), .e(decimal_decoder_4_p2_2[27]), .d(decimal_decoder_4_p2_2[26]),
    .c(decimal_decoder_4_p2_2[25]), .dp(decimal_decoder_4_p2_2[24]));
  _7_Segment_Display u_7_segment_display_12 (
    .g(decimal_decoder_4_p2[7]), .f(decimal_decoder_4_p2[6]), .a(decimal_decoder_4_p2[5]),
    .b(decimal_decoder_4_p2[4]), .e(decimal_decoder_4_p2_2[23]), .d(decimal_decoder_4_p2_2[22]),
    .c(decimal_decoder_4_p2_2[21]), .dp(decimal_decoder_4_p2_2[20]));
  _7_Segment_Display u_7_segment_display_13 (
    .g(decimal_decoder_4_p2[3]), .f(decimal_decoder_4_p2[2]), .a(decimal_decoder_4_p2[1]),
    .b(decimal_decoder_4_p2[0]), .e(decimal_decoder_4_p2_2[19]), .d(decimal_decoder_4_p2_2[18]),
    .c(decimal_decoder_4_p2_2[17]), .dp(decimal_decoder_4_p2_2[16]));
  assign bit_extender_2_out = {{5{1'b0}}, SC_O};  // Bit_Extender bit_extender_2
  assign MAR_p5 = in_1 ? in_2 : 4'bz;  // Controlled_Buffer controlled_buffer_4
  LED led_9 (.in(A_p2[7]));
  LED led_10 (.in(A_p2[6]));
  LED led_11 (.in(A_p2[5]));
  // CU cu_1: pin names not known; wires that end beside it: bitselector_2_out[3], bitselector_2_out[2], bitselector_2_out[1], bitselector_2_out[0], SC_O[2], SC_O[1], SC_O[0], cu_1_p8, cu_1_p9, cu_1_p10, cu_1_p11, MBR_p3, cu_1_p13, MBR_p2, A_p1, cu_1_p16, MAR_p2
  // Decimal_Decoder decimal_decoder_5: pin names not known; wires that end beside it: bit_extender_2_out, {decimal_decoder_5_p2_2, decimal_decoder_5_p2}, MAR_p3, alu_1_p3, A_p4, B_p2, OUTPUT_REGISTER_p2, OUTPUT_REGISTER_p3
  LED led_12 (.in(A_p2[4]));
  _7_Segment_Display u_7_segment_display_14 (
    .g(decimal_decoder_5_p2[3]), .f(decimal_decoder_5_p2[2]), .a(decimal_decoder_5_p2[1]),
    .b(decimal_decoder_5_p2[0]), .e(decimal_decoder_5_p2_2[3]), .d(decimal_decoder_5_p2_2[2]),
    .c(decimal_decoder_5_p2_2[1]), .dp(decimal_decoder_5_p2_2[0]));
  LED led_13 (.in(A_p2[3]));
  LED led_14 (.in(A_p2[2]));
  LED led_15 (.in(A_p2[1]));
  LED led_16 (.in(A_p2[0]));
  RAM #(.addrWidth(4), .enables("line")) ram_1 (
    .addr(MAR_p5), .we(cu_1_p10), .clk(CLK_out), .din(A_p2), .dout(ram_1_dout));
  assign A_p2 = cu_1_p11 ? ram_1_dout : 8'bz;  // Controlled_Buffer controlled_buffer_5

  // Notes on the sheet:
  //   OE
  //   WE
  //   INTERNAL ADDRESS BUS
  //   D7
  //   D5
  //   D6
  //   D4
  //   D3
  //   D2
  //   D1
  //   OE
  //   WE
  //   INTERNAL DATA BUS
  //   D0
  //   EXTERNAL ADDRESS BUS
  //   oe_test
  //   D7
  //   D5
  //   D6
  //   D4
  //   D3
  //   D2
  //   D1
  //   WE
  //   EXTERNAL DATA BUS
  //   D0
  //   OE
endmodule
